# Fritzing sketch cane-blind-proximity (saved by Fritzing 0.9.3b)

parts:
  Εξάρτημα1 = Arduino Uno (Rev3)
  VCC1 = Battery block 9V
  S1 = Taiway 100-SP-X-T1 SPDT Miniature Toggle Switch [part_number=100-SP-X-T1-0-0-B1-M1 package=THT]
  J1 = Piezo Speaker
  J2 = Basic Servo
  hc-sr1 = hc-sr04
  hc-sr2 = hc-sr04
  M1 = fc-51 [package=THT]

nets:
  N1: Εξάρτημα1.D9_PWM, hc-sr1.Trig
  N2: Εξάρτημα1.D10_PWM/SS, hc-sr1.Echo
  N3: Εξάρτημα1.D11_PWM/MOSI, hc-sr2.Echo
  N4: Εξάρτημα1.D12/MISO, hc-sr2.Trig
  N5: Εξάρτημα1.D13/SCK, J1.pin2
  GND: Εξάρτημα1.GND, VCC1.-, J1.pin1, J2.gnd, M1.pin2
  N6: Εξάρτημα1.D3_PWM, J2.pulse
  N7: Εξάρτημα1.D5_PWM, M1.pin1
  VCC: Εξάρτημα1.5V, J2.vcc, hc-sr1.VCC, M1.pin3
  N8: Εξάρτημα1.VIN, S1.L1
  N9: VCC1.+, S1.L2
