# Fritzing sketch sensor1-test (saved by Fritzing 0.9.3b)

parts:
  Εξάρτημα1 = Arduino Uno (Rev3)
  VCC1 = Battery block 9V
  S1 = Taiway 100-SP-X-T1 SPDT Miniature Toggle Switch [part_number=100-SP-X-T1-0-0-B1-M1 package=THT]
  J2 = Basic Servo
  hc-sr1 = hc-sr04

nets:
  N1: Εξάρτημα1.D9_PWM, hc-sr1.Trig
  N2: Εξάρτημα1.D10_PWM/SS, hc-sr1.Echo
  N3: Εξάρτημα1.D3_PWM, J2.pulse
  5V: Εξάρτημα1.5V, J2.vcc
  GND: Εξάρτημα1.GND, VCC1.-, J2.gnd, hc-sr1.GND
  N4: Εξάρτημα1.VIN, S1.L1
  N5: VCC1.+, S1.L2
