# Fritzing sketch sensor2-test (saved by Fritzing 0.9.3b)

parts:
  Εξάρτημα1 = Arduino Uno (Rev3)
  VCC1 = Battery block 9V
  S1 = Taiway 100-SP-X-T1 SPDT Miniature Toggle Switch [part_number=100-SP-X-T1-0-0-B1-M1 package=THT]
  J1 = Piezo Speaker
  hc-sr2 = hc-sr04

nets:
  N1: Εξάρτημα1.D11_PWM/MOSI, hc-sr2.Echo
  N2: Εξάρτημα1.D12/MISO, hc-sr2.Trig
  N3: Εξάρτημα1.D13/SCK, J1.pin2
  GND: Εξάρτημα1.GND, VCC1.-, J1.pin1, hc-sr2.GND
  5V: Εξάρτημα1.5V, hc-sr2.VCC
  N4: Εξάρτημα1.VIN, S1.L1
  N5: VCC1.+, S1.L2
