# Fritzing sketch sensor3-test (saved by Fritzing 0.9.3b)

parts:
  Εξάρτημα1 = Arduino Uno (Rev3)
  VCC1 = Battery block 9V
  S1 = Taiway 100-SP-X-T1 SPDT Miniature Toggle Switch [part_number=100-SP-X-T1-0-0-B1-M1 package=THT]
  J1 = Piezo Speaker
  M1 = fc-51 [package=THT]

nets:
  N1: Εξάρτημα1.D13/SCK, J1.pin2
  N2: Εξάρτημα1.GND, VCC1.-, J1.pin1, M1.pin2
  N3: Εξάρτημα1.D5_PWM, M1.pin1
  N4: Εξάρτημα1.5V, M1.pin3
  N5: Εξάρτημα1.VIN, S1.L1
  N6: VCC1.+, S1.L2
